# Fritzing sketch botonesWebArduino (saved by Fritzing 0.9.3b)

parts:
  Componente1 = Arduino Uno (Rev3)
  Squix1 = OLED 0.96" 128x64 I2C SSD1306

nets:
  N1: Componente1.A4/SDA, Squix1.SCA
  N2: Componente1.A5/SCL, Squix1.SCL
  5V: Componente1.5V, Squix1.VCC
  GND: Componente1.GND, Squix1.GND
